# Fritzing sketch solarWiring (saved by Fritzing 0.9.3b)
breadboards: 1

parts:
  R1 = Resistor [tolerance=±5% resistance=10k package=THT]
  R2 = Resistor [tolerance=±5% resistance=10k package=THT]
  R3 = Resistor [tolerance=±5% resistance=10k package=THT]
  Q1 = Basic FET P-Channel [package="TO220 [THT]"]
  D1 = SOLAR-IXYS [package=so08]

nets:
  GND: R1.Pin_0, R3.Pin_1, D1.A
  Solar Voltage pin: R1.Pin_1, R2.Pin_1
  N1: R2.Pin_0, Q1.source, D1.C
  solar Enable pin: R3.Pin_0, Q1.gate
  5V: Q1.drain
