# Fritzing sketch solarWiring (saved by Fritzing 0.9.3b)
breadboards: 1

parts:
  Q1 = Basic FET N-Channel [package="D2Pak [SMD]"]
  V1 = DC Power [voltage=5]
  R1 = Resistor [tolerance=±5% resistance=220 package=THT]
  R2 = Resistor [tolerance=±5% resistance=220 package=THT]
  U1 = Voltage Regulator - 5V [package="TO220 [THT]"]

nets:
  charge control pin: Q1.Gate
  GND: Q1.drain
  N1: Q1.source, V1.V-, R2.Pin_1, U1.GND
  N2: V1.V+, R1.Pin_1, U1.input_voltage
  Analog Pin: R1.Pin_0, R2.Pin_0
  5V: U1.output_voltage
